# Fritzing sketch DO_NHIET_DO (saved by Fritzing 0.9.2b)
circuit board: 10cm x 6.509cm
breadboards: 1

parts:
  Part1 = Arduino Nano (Rev3.0)
  U1 = Voltage Regulator - 5V [package="TO220 [THT]"]
  C1 = Electrolytic Capacitor [capacitance=1µF package="100 mil [THT, electrolytic]"]
  R1 = Resistor [tolerance=±5% resistance=220 package=THT]
  LED1 = LED - 5mm [color="Red (633nm)" package="5 mm [THT]"]
  NGUON = screw terminal, 2 pins
  R2 = Resistor [tolerance=±5% resistance=220 package=THT]
  R3 = Resistor [tolerance=±5% resistance=220 package=THT]
  R4 = Resistor [tolerance=±5% resistance=220 package=THT]
  R5 = Resistor [tolerance=±5% resistance=220 package=THT]
  NUT_XUONG = Momentary Switch [package=tactile-pth]
  NUT_CHON = Momentary Switch [package=tactile-pth]
  NUT_THOAT = Momentary Switch [package=tactile-pth]
  NUT_LEN = Momentary Switch [package=tactile-pth]
  SG1 = Buzzer 12mm [package=buzzer-12mm-ns]
  R6 = Resistor [tolerance=±5% resistance=220 package=THT]
  Nokia_5110_LCD_Module1 = Nokia 5110 LCD  # not connected

nets:
  GND: Part1.GND, U1.GND, C1.-, LED1.cathode, NGUON.pin2, NUT_XUONG.1, NUT_XUONG.2, NUT_CHON.1, NUT_CHON.2, NUT_THOAT.1, NUT_THOAT.2, NUT_LEN.1, NUT_LEN.2, SG1.2
  D3: Part1.D3, R6.Pin_0
  5V: Part1.VIN, Part1.5V, U1.output_voltage, C1.+, R1.Pin_0, R2.Pin_0, R3.Pin_0, R4.Pin_0, R5.Pin_0
  3V3: Part1.3V3
  N1: U1.input_voltage, NGUON.pin1
  N2: R1.Pin_1, LED1.anode
  N3: R2.Pin_1, NUT_XUONG.4
  N4: R3.Pin_1, NUT_LEN.4
  N5: R4.Pin_1, NUT_CHON.4
  N6: R5.Pin_1, NUT_THOAT.4
  N7: SG1.1, R6.Pin_1

custom parts:
  Nokia 5110 LCD: Nokia 5110 Graphic 84*48 LCD module <Blue Version>
